# Fritzing sketch CircuitDiagram (saved by Fritzing 0.9.3b)
breadboards: 1

parts:
  HC-SR04_Sensor_1 = HC-SR04 Ultrasonic Distance Sensor
  HC-SR04_Sensor_2 = HC-SR04 Ultrasonic Distance Sensor
  Part1 = Arduino Uno (Rev3)

nets:
  VCC: HC-SR04_Sensor_1.VCC, HC-SR04_Sensor_2.VCC, Part1.5V
  N1: HC-SR04_Sensor_1.TRIG, Part1.D2
  N2: HC-SR04_Sensor_1.ECHO, Part1.D6_PWM
  GND: HC-SR04_Sensor_1.GND, HC-SR04_Sensor_2.GND, Part1.GND
  N3: HC-SR04_Sensor_2.TRIG, Part1.D4
  N4: HC-SR04_Sensor_2.ECHO, Part1.D8
